// Logisim project CA10MIPS.circ as structural Verilog: 8 circuits, main circuit TG00MIPS
module TG00MIPS (
  output halt
);

  wire clock_1_out, or_1_out;

  Clock clock_1 (.out(clock_1_out));
  or or_1 (or_1_out, halt, clock_1_out);
  MIPS MIPS (.clk(or_1_out), .reset(1'b0), .halt(halt));

  // Notes on the sheet:
  //   No modificar esta hoja !!!
endmodule

module MIPS (
  input  clk,
  input  reset,
  output halt
);

  wire FB, FC, FDC, IB0, IB1, IB2, IB3, IB4, IB5, IB6, IB7, IB8, IB9, IB10, IB11, IB12, IB13, IB14, IB15,
       IB16, IB17, IB18, IB19, IB20, IB21, IB22, IB23, IB24, IB25, IB26, IB27, IB28, IB29, IB30, IB31, RM,
       WM, WR, Z;
  wire [1:0] FPC;
  wire [2:0] OPALU;
  wire [3:0] alucontrol_1_op;
  wire [4:0] multiplexer_2_out;
  wire [25:0] shifter_1_out;
  wire [31:0] alu_1_result, AS2, bit_extender_1_out, data_memory_32_1_read_data, MPLX, multiplexer_1_out,
       multiplexer_3_out, multiplexer_4_out, PC_q, register_file_1_read_data_1, register_file_1_read_data_2,
       shifter_2_out;

  Register #(.width(32)) PC (.D(multiplexer_1_out), .en(1'b1), .Q(PC_q), .clk(clk), .clr(reset));
  Multiplexer #(.select(2), .width(32), .enable("false")) multiplexer_1 (
    .in1({AS2[31:26], shifter_1_out}), .in2(MPLX), .in3(AS2), .out(multiplexer_1_out), .sel(FPC));  // open: in0
  Adder #(.width(32)) adder_1 (.a(32'h4), .b(PC_q), .out(AS2), .cin(1'b0));  // open: cout
  Instruction_memory instruction_memory_1 (
    .Read_address(PC_q),
    .Instruction({IB31, IB30, IB29, IB28, IB27, IB26, IB25, IB24, IB23, IB22, IB21, IB20, IB19, IB18, IB17, IB16, IB15, IB14, IB13, IB12, IB11, IB10, IB9, IB8, IB7, IB6, IB5, IB4, IB3, IB2, IB1, IB0}));
  Unidad_de_Control unidad_de_control_1 (
    .Opcode({IB31, IB30, IB29, IB28, IB27, IB26}), .z(Z), .FPC(FPC), .WR(WR), .FDC(FDC), .FC(FC), .FB(FB),
    .RM(RM), .WM(WM), .OPALU(OPALU), .halt(halt));
  Multiplexer #(.width(5), .enable("false")) multiplexer_2 (
    .in0({IB20, IB19, IB18, IB17, IB16}), .in1({IB15, IB14, IB13, IB12, IB11}), .out(multiplexer_2_out),
    .sel(FDC));
  Multiplexer #(.width(32), .enable("false")) multiplexer_3 (
    .in0(data_memory_32_1_read_data), .in1(alu_1_result), .out(multiplexer_3_out), .sel(FC));
  assign bit_extender_1_out = {{16{IB15}}, {IB15, IB14, IB13, IB12, IB11, IB10, IB9, IB8, IB7, IB6, IB5, IB4, IB3, IB2, IB1, IB0}};  // Bit_Extender bit_extender_1
  Register_file register_file_1 (
    .Read_Register_1({IB25, IB24, IB23, IB22, IB21}), .Read_Register_2({IB20, IB19, IB18, IB17, IB16}),
    .Write_Register(multiplexer_2_out), .Write_Data(multiplexer_3_out),
    .Read_Data_1(register_file_1_read_data_1), .Read_Data_2(register_file_1_read_data_2), .clk(clk),
    .reset(reset), .Write(WR));
  Shifter #(.width(26)) shifter_1 (
    .in({IB25, IB24, IB23, IB22, IB21, IB20, IB19, IB18, IB17, IB16, IB15, IB14, IB13, IB12, IB11, IB10, IB9, IB8, IB7, IB6, IB5, IB4, IB3, IB2, IB1, IB0}),
    .\dist (5'b00010), .out(shifter_1_out));
  Shifter #(.width(32)) shifter_2 (.in(bit_extender_1_out), .\dist (5'b00010), .out(shifter_2_out));
  Multiplexer #(.width(32), .enable("false")) multiplexer_4 (
    .in0(register_file_1_read_data_2), .in1(bit_extender_1_out), .out(multiplexer_4_out), .sel(FB));
  Adder #(.width(32)) adder_2 (.a(AS2), .b(shifter_2_out), .out(MPLX));  // open: cin, cout
  AluControl alucontrol_1 (.IB_5_0({IB5, IB4, IB3, IB2, IB1, IB0}), .Opalu(OPALU), .Op(alucontrol_1_op));
  ALU alu_1 (
    .A(register_file_1_read_data_1), .B(multiplexer_4_out), .Z(Z), .Result(alu_1_result),
    .Operation(alucontrol_1_op));
  Data_Memory_32 data_memory_32_1 (
    .Address(alu_1_result), .Write_Data(register_file_1_read_data_2), .Read_Data(data_memory_32_1_read_data),
    .Write(WM), .clk(clk), .reset(reset), .Read(RM));

  // Other names for the same wires on the sheet: PC4_26 = AS2[26]; PC4_27 = AS2[27]; PC4_28 = AS2[28];
  //   PC4_29 = AS2[29]; PC4_30 = AS2[30]; PC4_31 = AS2[31]
endmodule

module Register_file (
  input  clk,
  input  reset,
  input  [4:0] Read_Register_1,
  input  [4:0] Read_Register_2,
  input  [4:0] Write_Register,
  input  [31:0] Write_Data,
  input  Write,
  output [31:0] Read_Data_1,
  output [31:0] Read_Data_2
);

  wire decoder_1_out1, decoder_1_out2, decoder_1_out3, decoder_1_out4, decoder_1_out5, decoder_1_out6,
       decoder_1_out7, decoder_1_out8, decoder_1_out9, decoder_1_out10, decoder_1_out11, decoder_1_out12,
       decoder_1_out13, decoder_1_out14, decoder_1_out15, decoder_1_out16, decoder_1_out17, decoder_1_out18,
       decoder_1_out19, decoder_1_out20, decoder_1_out21, decoder_1_out22, decoder_1_out23, decoder_1_out24,
       decoder_1_out25, decoder_1_out26, decoder_1_out27, decoder_1_out28, decoder_1_out29, decoder_1_out30,
       decoder_1_out31;
  wire [31:0] R1_q, R2_q, R3_q, R4_q, R5_q, R6_q, R7_q, R8_q, R9_q, R10_q, R11_q, R12_q, R13_q, R14_q, R15_q,
       R16_q, R17_q, R18_q, R19_q, R20_q, R21_q, R22_q, R23_q, R24_q, R25_q, R26_q, R27_q, R28_q, R29_q,
       R30_q, R31_q;

  Decoder #(.select(5), .disabled(0)) decoder_1 (
    .out1(decoder_1_out1), .out2(decoder_1_out2), .out3(decoder_1_out3), .out4(decoder_1_out4),
    .out5(decoder_1_out5), .out6(decoder_1_out6), .out7(decoder_1_out7), .out8(decoder_1_out8),
    .out9(decoder_1_out9), .out10(decoder_1_out10), .out11(decoder_1_out11), .out12(decoder_1_out12),
    .out13(decoder_1_out13), .out14(decoder_1_out14), .out15(decoder_1_out15), .out16(decoder_1_out16),
    .out17(decoder_1_out17), .out18(decoder_1_out18), .out19(decoder_1_out19), .out20(decoder_1_out20),
    .out21(decoder_1_out21), .out22(decoder_1_out22), .out23(decoder_1_out23), .out24(decoder_1_out24),
    .out25(decoder_1_out25), .out26(decoder_1_out26), .out27(decoder_1_out27), .out28(decoder_1_out28),
    .out29(decoder_1_out29), .out30(decoder_1_out30), .out31(decoder_1_out31), .sel(Write_Register),
    .en(Write));  // open: out0
  Register #(.width(32)) R1 (.D(Write_Data), .en(decoder_1_out1), .Q(R1_q), .clk(clk), .clr(reset));
  Register #(.width(32)) R2 (.D(Write_Data), .en(decoder_1_out2), .Q(R2_q), .clk(clk), .clr(reset));
  Register #(.width(32)) R3 (.D(Write_Data), .en(decoder_1_out3), .Q(R3_q), .clk(clk), .clr(reset));
  Register #(.width(32)) R4 (.D(Write_Data), .en(decoder_1_out4), .Q(R4_q), .clk(clk), .clr(reset));
  Register #(.width(32)) R5 (.D(Write_Data), .en(decoder_1_out5), .Q(R5_q), .clk(clk), .clr(reset));
  Register #(.width(32)) R6 (.D(Write_Data), .en(decoder_1_out6), .Q(R6_q), .clk(clk), .clr(reset));
  Register #(.width(32)) R7 (.D(Write_Data), .en(decoder_1_out7), .Q(R7_q), .clk(clk), .clr(reset));
  Register #(.width(32)) R8 (.D(Write_Data), .en(decoder_1_out8), .Q(R8_q), .clk(clk), .clr(reset));
  Register #(.width(32)) R9 (.D(Write_Data), .en(decoder_1_out9), .Q(R9_q), .clk(clk), .clr(reset));
  Register #(.width(32)) R10 (.D(Write_Data), .en(decoder_1_out10), .Q(R10_q), .clk(clk), .clr(reset));
  Register #(.width(32)) R11 (.D(Write_Data), .en(decoder_1_out11), .Q(R11_q), .clk(clk), .clr(reset));
  Register #(.width(32)) R12 (.D(Write_Data), .en(decoder_1_out12), .Q(R12_q), .clk(clk), .clr(reset));
  Register #(.width(32)) R13 (.D(Write_Data), .en(decoder_1_out13), .Q(R13_q), .clk(clk), .clr(reset));
  Register #(.width(32)) R14 (.D(Write_Data), .en(decoder_1_out14), .Q(R14_q), .clk(clk), .clr(reset));
  Register #(.width(32)) R15 (.D(Write_Data), .en(decoder_1_out15), .Q(R15_q), .clk(clk), .clr(reset));
  Register #(.width(32)) R16 (.D(Write_Data), .en(decoder_1_out16), .Q(R16_q), .clk(clk), .clr(reset));
  Register #(.width(32)) R17 (.D(Write_Data), .en(decoder_1_out17), .Q(R17_q), .clk(clk), .clr(reset));
  Register #(.width(32)) R18 (.D(Write_Data), .en(decoder_1_out18), .Q(R18_q), .clk(clk), .clr(reset));
  Register #(.width(32)) R19 (.D(Write_Data), .en(decoder_1_out19), .Q(R19_q), .clk(clk), .clr(reset));
  Register #(.width(32)) R20 (.D(Write_Data), .en(decoder_1_out20), .Q(R20_q), .clk(clk), .clr(reset));
  Register #(.width(32)) R21 (.D(Write_Data), .en(decoder_1_out21), .Q(R21_q), .clk(clk), .clr(reset));
  Register #(.width(32)) R22 (.D(Write_Data), .en(decoder_1_out22), .Q(R22_q), .clk(clk), .clr(reset));
  Register #(.width(32)) R23 (.D(Write_Data), .en(decoder_1_out23), .Q(R23_q), .clk(clk), .clr(reset));
  Register #(.width(32)) R24 (.D(Write_Data), .en(decoder_1_out24), .Q(R24_q), .clk(clk), .clr(reset));
  Register #(.width(32)) R25 (.D(Write_Data), .en(decoder_1_out25), .Q(R25_q), .clk(clk), .clr(reset));
  Register #(.width(32)) R26 (.D(Write_Data), .en(decoder_1_out26), .Q(R26_q), .clk(clk), .clr(reset));
  Register #(.width(32)) R27 (.D(Write_Data), .en(decoder_1_out27), .Q(R27_q), .clk(clk), .clr(reset));
  Register #(.width(32)) R28 (.D(Write_Data), .en(decoder_1_out28), .Q(R28_q), .clk(clk), .clr(reset));
  Register #(.width(32)) R29 (.D(Write_Data), .en(decoder_1_out29), .Q(R29_q), .clk(clk), .clr(reset));
  Register #(.width(32)) R30 (.D(Write_Data), .en(decoder_1_out30), .Q(R30_q), .clk(clk), .clr(reset));
  Register #(.width(32)) R31 (.D(Write_Data), .en(decoder_1_out31), .Q(R31_q), .clk(clk), .clr(reset));
  Multiplexer #(.select(5), .width(32), .enable("false")) multiplexer_1 (
    .in0({32{1'b0}}), .in1(R1_q), .in2(R2_q), .in3(R3_q), .in4(R4_q), .in5(R5_q), .in6(R6_q), .in7(R7_q),
    .in8(R8_q), .in9(R9_q), .in10(R10_q), .in11(R11_q), .in12(R12_q), .in13(R13_q), .in14(R14_q),
    .in15(R15_q), .in16(R16_q), .in17(R17_q), .in18(R18_q), .in19(R19_q), .in20(R20_q), .in21(R21_q),
    .in22(R22_q), .in23(R23_q), .in24(R24_q), .in25(R25_q), .in26(R26_q), .in27(R27_q), .in28(R28_q),
    .in29(R29_q), .in30(R30_q), .in31(R31_q), .out(Read_Data_1), .sel(Read_Register_1));
  Multiplexer #(.select(5), .width(32), .enable("false")) multiplexer_2 (
    .in0({32{1'b0}}), .in1(R1_q), .in2(R2_q), .in3(R3_q), .in4(R4_q), .in5(R5_q), .in6(R6_q), .in7(R7_q),
    .in8(R8_q), .in9(R9_q), .in10(R10_q), .in11(R11_q), .in12(R12_q), .in13(R13_q), .in14(R14_q),
    .in15(R15_q), .in16(R16_q), .in17(R17_q), .in18(R18_q), .in19(R19_q), .in20(R20_q), .in21(R21_q),
    .in22(R22_q), .in23(R23_q), .in24(R24_q), .in25(R25_q), .in26(R26_q), .in27(R27_q), .in28(R28_q),
    .in29(R29_q), .in30(R30_q), .in31(R31_q), .out(Read_Data_2), .sel(Read_Register_2));
endmodule

module ALU (
  input  [3:0] Operation,
  input  [31:0] A,
  input  [31:0] B,
  output Z,
  output [31:0] Result
);

  wire [0:0] comparator_1_lt;
  wire [31:0] adder_1_out, and_1_out, multiplexer_1_out, multiplexer_2_out, not_1_out, not_2_out, or_1_out;

  assign not_1_out = ~A;  // NOT_Gate not_1, 32 bits wide
  assign not_2_out = ~B;  // NOT_Gate not_2, 32 bits wide
  Comparator #(.width(32)) comparator_1 (.a(A), .b(B), .lt(comparator_1_lt[0]));  // open: gt, eq
  Multiplexer #(.width(32), .enable("false")) multiplexer_1 (
    .in0(A), .in1(not_1_out), .out(multiplexer_1_out), .sel(Operation[3]));
  Multiplexer #(.width(32), .enable("false")) multiplexer_2 (
    .in0(B), .in1(not_2_out), .out(multiplexer_2_out), .sel(Operation[2]));
  assign and_1_out = multiplexer_1_out & multiplexer_2_out;  // AND_Gate and_1, 32 bits wide
  assign or_1_out = multiplexer_1_out | multiplexer_2_out;  // OR_Gate or_1, 32 bits wide
  Adder #(.width(32)) adder_1 (
    .a(multiplexer_1_out), .b(multiplexer_2_out), .out(adder_1_out), .cin(Operation[2]));  // open: cout
  Multiplexer #(.select(2), .width(32), .enable("false")) multiplexer_3 (
    .in0(and_1_out), .in1(or_1_out), .in2(adder_1_out), .in3({{31{1'b0}}, comparator_1_lt[0]}), .out(Result),
    .sel(Operation[1:0]));
  nor nor_1 (Z, Result[0], Result[1], Result[2], Result[3], Result[4], Result[5], Result[6], Result[7], Result[8], Result[9], Result[10], Result[11], Result[12], Result[13], Result[14], Result[15], Result[16], Result[17], Result[18], Result[19], Result[20], Result[21], Result[22], Result[23], Result[24], Result[25], Result[26], Result[27], Result[28], Result[29], Result[30], Result[31]);

  // Notes on the sheet:
  //   0001    OR
  //   Operation    Function
  //   0000    AND
  //   0010    add
  //   0110    subtract
  //   0111    set on less than
  //   1100    NOR
endmodule

module Data_Memory_32 (
  input  Write,
  input  [31:0] Address,
  input  [31:0] Write_Data,
  input  clk,
  input  reset,
  input  Read,
  output [31:0] Read_Data
);

  wire [9:0] bitselector_1_out;

  BitSelector #(.width(32), .group(10)) bitselector_1 (.in(Address), .out(bitselector_1_out), .sel(2'b00));
  RAM #(.dataWidth(32), .bus("separate"), .Datafile_on_reset("TG00ram.txt")) ram_1 (
    .addr(bitselector_1_out[9:2]), .din(Write_Data), .data(Read_Data), .str(Write), .sel(1'b1), .clk(clk),
    .ld(Read), .clr(reset));

  // Notes on the sheet:
  //   Memoria de 32 bits direccionable a nivel de byte
  //   Tan solo implementadas las 256 primeras posiciones de 32 bits o 1024 bytes
endmodule

module Instruction_memory (
  input  [31:0] Read_address,
  output [31:0] Instruction
);

  wire [6:0] bitselector_1_out;

  BitSelector #(.width(30), .group(7)) bitselector_1 (.in(Read_address[31:2]), .out(bitselector_1_out), .sel(3'b000));
  RAM #(.addrWidth(7), .dataWidth(32), .bus("asynch"), .Datafile_on_reset("TG00rom.txt")) ram_1 (
    .addr(bitselector_1_out), .data(Instruction), .sel(1'b1), .ld(1'b1), .clr(1'b0));
endmodule

module AluControl (
  input  [5:0] IB_5_0,
  input  [2:0] Opalu,
  output [3:0] Op
);

  wire [1:0] or_1_out;
  wire [2:1] not_1_out;

  and and_1 (not_1_out[2], ~Opalu[1], Opalu[0]);  // AND_Gate
  not not_1 (not_1_out[1], Opalu[1]);
  not not_2 (or_1_out[1], IB_5_0[2]);
  or or_1 (or_1_out[0], IB_5_0[0], IB_5_0[3]);
  Multiplexer #(.width(4), .enable("false")) multiplexer_1 (
    .in0({1'b0, not_1_out, Opalu[1]}), .in1({1'b0, IB_5_0[1], or_1_out}), .out(Op), .sel(Opalu[2]));
endmodule

module Unidad_de_Control (
  input  [5:0] Opcode,
  input  z,
  output [1:0] FPC,
  output WR,
  output FDC,
  output FC,
  output FB,
  output RM,
  output WM,
  output [2:0] OPALU,
  output halt
);

  wire and_1_out, and_2_out;

  or or_1 (FPC[1], Opcode[0], ~Opcode[1]);  // OR_Gate
  and and_1 (and_1_out, Opcode[0], ~Opcode[3]);  // AND_Gate
  nand nand_1 (FPC[0], z, Opcode[2]);
  and and_2 (and_2_out, ~Opcode[2], ~Opcode[1]);  // AND_Gate
  or or_2 (WR, and_1_out, and_2_out);
  not not_1 (FC, Opcode[1]);
  and and_3 (FB, Opcode[1], ~Opcode[4]);  // AND_Gate
  not not_2 (RM, Opcode[3]);
  and and_4 (WM, Opcode[3], ~Opcode[4]);  // AND_Gate
  and and_5 (OPALU[1], ~Opcode[5], ~Opcode[2]);  // AND_Gate
  and and_6 (OPALU[2], ~Opcode[5], ~Opcode[2]);  // AND_Gate
  not not_3 (OPALU[0], Opcode[1]);
  and and_7 (halt, Opcode[5], Opcode[4], Opcode[3], Opcode[2], Opcode[1], Opcode[0]);

  assign FDC = FC;
endmodule
