// Logisim project CA10MIPS.circ as structural Verilog: 11 circuits, main circuit TG00MIPS
module TG00MIPS (
  output halt
);

  wire clock_1_out, or_1_out;

  Clock clock_1 (.out(clock_1_out));
  or or_1 (or_1_out, halt, clock_1_out);
  MIPS MIPS (.clk(or_1_out), .reset(1'b0), .halt(halt));

  // Notes on the sheet:
  //   No modificar esta hoja !!!
endmodule

module MIPS (
  input  clk,
  input  reset,
  output halt
);

  wire Especial, FB, FC, FDC, IB0, IB1, IB2, IB3, IB4, IB5, IB6, IB7, IB8, IB9, IB10, IB11, IB12, IB13, IB14,
       IB15, IB16, IB17, IB18, IB19, IB20, IB21, IB22, IB23, IB24, IB25, IB26, IB27, IB28, IB29, IB30, IB31,
       RM, WM, WR, Z;
  wire [1:0] FPC;
  wire [2:0] OPALU;
  wire [3:0] alucontrol_1_op;
  wire [4:0] multiplexer_2_out;
  wire [25:0] shifter_1_out;
  wire [31:0] alu_1_result, AS2, bit_extender_1_out, data_memory_32_1_read_data, MPLX, multiplexer_1_out,
       multiplexer_3_out, multiplexer_4_out, PC_q, register_file_1_read_data_1, register_file_1_read_data_2,
       shifter_2_out;

  Register #(.width(32)) PC (.D(multiplexer_1_out), .en(1'b1), .Q(PC_q), .clk(clk), .clr(reset));
  Multiplexer #(.select(2), .width(32), .enable("false")) multiplexer_1 (
    .in1({AS2[31:26], shifter_1_out}), .in2(MPLX), .in3(AS2), .out(multiplexer_1_out), .sel(FPC));  // open: in0
  Adder #(.width(32)) adder_1 (.a(32'h4), .b(PC_q), .out(AS2), .cin(1'b0));  // open: cout
  Instruction_memory instruction_memory_1 (
    .Read_address(PC_q),
    .Instruction({IB31, IB30, IB29, IB28, IB27, IB26, IB25, IB24, IB23, IB22, IB21, IB20, IB19, IB18, IB17, IB16, IB15, IB14, IB13, IB12, IB11, IB10, IB9, IB8, IB7, IB6, IB5, IB4, IB3, IB2, IB1, IB0}));
  UCPr2 ucpr2_1 (
    .Opcode({IB31, IB30, IB29, IB28, IB27, IB26}), .Z(Z), .halt(halt), .FPC(FPC), .WR(WR), .FDC(FDC),
    .FC(FC), .FB(FB), .RM(RM), .WM(WM), .OpAlu(OPALU), .ESPECIAL(Especial));
  Multiplexer #(.width(5), .enable("false")) multiplexer_2 (
    .in0({IB20, IB19, IB18, IB17, IB16}), .in1({IB15, IB14, IB13, IB12, IB11}), .out(multiplexer_2_out),
    .sel(FDC));
  Multiplexer #(.width(32), .enable("false")) multiplexer_3 (
    .in0(data_memory_32_1_read_data), .in1(alu_1_result), .out(multiplexer_3_out), .sel(FC));
  assign bit_extender_1_out = {{16{IB15}}, {IB15, IB14, IB13, IB12, IB11, IB10, IB9, IB8, IB7, IB6, IB5, IB4, IB3, IB2, IB1, IB0}};  // Bit_Extender bit_extender_1
  Register_file register_file_1 (
    .Read_Register_1({IB25, IB24, IB23, IB22, IB21}), .Read_Register_2({IB20, IB19, IB18, IB17, IB16}),
    .Write_Register(multiplexer_2_out), .Write_Data(multiplexer_3_out),
    .Read_Data_1(register_file_1_read_data_1), .Read_Data_2(register_file_1_read_data_2), .clk(clk),
    .reset(reset), .Write(WR), .Especial(Especial));
  Shifter #(.width(26)) shifter_1 (
    .in({IB25, IB24, IB23, IB22, IB21, IB20, IB19, IB18, IB17, IB16, IB15, IB14, IB13, IB12, IB11, IB10, IB9, IB8, IB7, IB6, IB5, IB4, IB3, IB2, IB1, IB0}),
    .\dist (5'b00010), .out(shifter_1_out));
  Shifter #(.width(32)) shifter_2 (.in(bit_extender_1_out), .\dist (5'b00010), .out(shifter_2_out));
  Multiplexer #(.width(32), .enable("false")) multiplexer_4 (
    .in0(register_file_1_read_data_2), .in1(bit_extender_1_out), .out(multiplexer_4_out), .sel(FB));
  Adder #(.width(32)) adder_2 (.a(AS2), .b(shifter_2_out), .out(MPLX));  // open: cin, cout
  AluControl alucontrol_1 (.IB_5_0({IB5, IB4, IB3, IB2, IB1, IB0}), .Opalu(OPALU), .Op(alucontrol_1_op));
  ALU alu_1 (
    .A(register_file_1_read_data_1), .B(multiplexer_4_out), .Z(Z), .Result(alu_1_result),
    .Operation(alucontrol_1_op));
  Data_Memory_32 data_memory_32_1 (
    .Address(alu_1_result), .Write_Data(register_file_1_read_data_2), .Read_Data(data_memory_32_1_read_data),
    .Write(WM), .clk(clk), .reset(reset), .Read(RM));

  // Other names for the same wires on the sheet: PC4_26 = AS2[26]; PC4_27 = AS2[27]; PC4_28 = AS2[28];
  //   PC4_29 = AS2[29]; PC4_30 = AS2[30]; PC4_31 = AS2[31]
endmodule

module Register_file (
  input  clk,
  input  reset,
  input  [4:0] Read_Register_1,
  input  [4:0] Read_Register_2,
  input  Especial,
  input  [4:0] Write_Register,
  input  [31:0] Write_Data,
  input  Write,
  output [31:0] Read_Data_1,
  output [31:0] Read_Data_2
);

  wire decoder_2_out1, decoder_2_out2, decoder_2_out3, decoder_2_out4, decoder_2_out5, decoder_2_out6,
       decoder_2_out7, decoder_2_out8, decoder_2_out9, decoder_2_out10, decoder_2_out11, decoder_2_out12,
       decoder_2_out13, decoder_2_out14, decoder_2_out15, decoder_2_out16, decoder_2_out17, decoder_2_out18,
       decoder_2_out19, decoder_2_out20, decoder_2_out21, decoder_2_out22, decoder_2_out23, decoder_2_out24,
       decoder_2_out25, decoder_2_out26, decoder_2_out27, decoder_2_out28, decoder_2_out29, decoder_2_out30,
       decoder_2_out31, r1, r2, r3, r4, r5, r6, r7, r8, r9, r10, r11, r12, r13, r14, r15, r16, r17, r18, r19,
       r20, r21, r22, r23, r24, r25, r26, r27, r28, r29, r30, r31;
  wire [31:0] R1_read_data_1, R2_read_data_1, R3_read_data_1, R4_read_data_1, R5_read_data_1, R6_read_data_1,
       R7_read_data_1, R8_read_data_1, R9_read_data_1, R10_read_data_1, R11_read_data_1, R12_read_data_1,
       R13_read_data_1, R14_read_data_1, R15_read_data_1, R16_read_data_1, R17_read_data_1, R18_read_data_1,
       R19_read_data_1, R20_read_data_1, R21_read_data_1, R22_read_data_1, R23_read_data_1, R24_read_data_1,
       R25_read_data_1, R26_read_data_1, R27_read_data_1, R28_read_data_1, R29_read_data_1, R30_read_data_1,
       R31_read_data_1;

  Decoder #(.select(5), .disabled(0)) decoder_1 (
    .out1(r1), .out2(r2), .out3(r3), .out4(r4), .out5(r5), .out6(r6), .out7(r7), .out8(r8), .out9(r9),
    .out10(r10), .out11(r11), .out12(r12), .out13(r13), .out14(r14), .out15(r15), .out16(r16), .out17(r17),
    .out18(r18), .out19(r19), .out20(r20), .out21(r21), .out22(r22), .out23(r23), .out24(r24), .out25(r25),
    .out26(r26), .out27(r27), .out28(r28), .out29(r29), .out30(r30), .out31(r31), .sel(Read_Register_1),
    .en(Especial));  // open: out0
  Decoder #(.select(5), .disabled(0)) decoder_2 (
    .out1(decoder_2_out1), .out2(decoder_2_out2), .out3(decoder_2_out3), .out4(decoder_2_out4),
    .out5(decoder_2_out5), .out6(decoder_2_out6), .out7(decoder_2_out7), .out8(decoder_2_out8),
    .out9(decoder_2_out9), .out10(decoder_2_out10), .out11(decoder_2_out11), .out12(decoder_2_out12),
    .out13(decoder_2_out13), .out14(decoder_2_out14), .out15(decoder_2_out15), .out16(decoder_2_out16),
    .out17(decoder_2_out17), .out18(decoder_2_out18), .out19(decoder_2_out19), .out20(decoder_2_out20),
    .out21(decoder_2_out21), .out22(decoder_2_out22), .out23(decoder_2_out23), .out24(decoder_2_out24),
    .out25(decoder_2_out25), .out26(decoder_2_out26), .out27(decoder_2_out27), .out28(decoder_2_out28),
    .out29(decoder_2_out29), .out30(decoder_2_out30), .out31(decoder_2_out31), .sel(Write_Register),
    .en(Write));  // open: out0
  Macro u_R1 (
    .Read_Register_1(Write_Data), .Especial(r1), .Write(decoder_2_out1), .clk(clk), .reset(reset),
    .Read_Data_1(R1_read_data_1));
  Macro u_R2 (
    .Read_Register_1(Write_Data), .Especial(r2), .Write(decoder_2_out2), .clk(clk), .reset(reset),
    .Read_Data_1(R2_read_data_1));
  Macro u_R3 (
    .Read_Register_1(Write_Data), .Especial(r3), .Write(decoder_2_out3), .clk(clk), .reset(reset),
    .Read_Data_1(R3_read_data_1));
  Macro u_R4 (
    .Read_Register_1(Write_Data), .Especial(r4), .Write(decoder_2_out4), .clk(clk), .reset(reset),
    .Read_Data_1(R4_read_data_1));
  Macro u_R5 (
    .Read_Register_1(Write_Data), .Especial(r5), .Write(decoder_2_out5), .clk(clk), .reset(reset),
    .Read_Data_1(R5_read_data_1));
  Macro u_R6 (
    .Read_Register_1(Write_Data), .Especial(r6), .Write(decoder_2_out6), .clk(clk), .reset(reset),
    .Read_Data_1(R6_read_data_1));
  Macro u_R7 (
    .Read_Register_1(Write_Data), .Especial(r7), .Write(decoder_2_out7), .clk(clk), .reset(reset),
    .Read_Data_1(R7_read_data_1));
  Macro u_R8 (
    .Read_Register_1(Write_Data), .Especial(r8), .Write(decoder_2_out8), .clk(clk), .reset(reset),
    .Read_Data_1(R8_read_data_1));
  Macro u_R9 (
    .Read_Register_1(Write_Data), .Especial(r9), .Write(decoder_2_out9), .clk(clk), .reset(reset),
    .Read_Data_1(R9_read_data_1));
  Macro u_R10 (
    .Read_Register_1(Write_Data), .Especial(r10), .Write(decoder_2_out10), .clk(clk), .reset(reset),
    .Read_Data_1(R10_read_data_1));
  Macro u_R11 (
    .Read_Register_1(Write_Data), .Especial(r11), .Write(decoder_2_out11), .clk(clk), .reset(reset),
    .Read_Data_1(R11_read_data_1));
  Macro u_R12 (
    .Read_Register_1(Write_Data), .Especial(r12), .Write(decoder_2_out12), .clk(clk), .reset(reset),
    .Read_Data_1(R12_read_data_1));
  Macro u_R13 (
    .Read_Register_1(Write_Data), .Especial(r13), .Write(decoder_2_out13), .clk(clk), .reset(reset),
    .Read_Data_1(R13_read_data_1));
  Macro u_R14 (
    .Read_Register_1(Write_Data), .Especial(r14), .Write(decoder_2_out14), .clk(clk), .reset(reset),
    .Read_Data_1(R14_read_data_1));
  Macro u_R15 (
    .Read_Register_1(Write_Data), .Especial(r15), .Write(decoder_2_out15), .clk(clk), .reset(reset),
    .Read_Data_1(R15_read_data_1));
  Macro u_R16 (
    .Read_Register_1(Write_Data), .Especial(r16), .Write(decoder_2_out16), .clk(clk), .reset(reset),
    .Read_Data_1(R16_read_data_1));
  Macro u_R17 (
    .Read_Register_1(Write_Data), .Especial(r17), .Write(decoder_2_out17), .clk(clk), .reset(reset),
    .Read_Data_1(R17_read_data_1));
  Macro u_R18 (
    .Read_Register_1(Write_Data), .Especial(r18), .Write(decoder_2_out18), .clk(clk), .reset(reset),
    .Read_Data_1(R18_read_data_1));
  Macro u_R19 (
    .Read_Register_1(Write_Data), .Especial(r19), .Write(decoder_2_out19), .clk(clk), .reset(reset),
    .Read_Data_1(R19_read_data_1));
  Macro u_R20 (
    .Read_Register_1(Write_Data), .Especial(r20), .Write(decoder_2_out20), .clk(clk), .reset(reset),
    .Read_Data_1(R20_read_data_1));
  Macro u_R21 (
    .Read_Register_1(Write_Data), .Especial(r21), .Write(decoder_2_out21), .clk(clk), .reset(reset),
    .Read_Data_1(R21_read_data_1));
  Macro u_R22 (
    .Read_Register_1(Write_Data), .Especial(r22), .Write(decoder_2_out22), .clk(clk), .reset(reset),
    .Read_Data_1(R22_read_data_1));
  Macro u_R23 (
    .Read_Register_1(Write_Data), .Especial(r23), .Write(decoder_2_out23), .clk(clk), .reset(reset),
    .Read_Data_1(R23_read_data_1));
  Macro u_R24 (
    .Read_Register_1(Write_Data), .Especial(r24), .Write(decoder_2_out24), .clk(clk), .reset(reset),
    .Read_Data_1(R24_read_data_1));
  Macro u_R25 (
    .Read_Register_1(Write_Data), .Especial(r25), .Write(decoder_2_out25), .clk(clk), .reset(reset),
    .Read_Data_1(R25_read_data_1));
  Macro u_R26 (
    .Read_Register_1(Write_Data), .Especial(r26), .Write(decoder_2_out26), .clk(clk), .reset(reset),
    .Read_Data_1(R26_read_data_1));
  Macro u_R27 (
    .Read_Register_1(Write_Data), .Especial(r27), .Write(decoder_2_out27), .clk(clk), .reset(reset),
    .Read_Data_1(R27_read_data_1));
  Macro u_R28 (
    .Read_Register_1(Write_Data), .Especial(r28), .Write(decoder_2_out28), .clk(clk), .reset(reset),
    .Read_Data_1(R28_read_data_1));
  Macro u_R29 (
    .Read_Register_1(Write_Data), .Especial(r29), .Write(decoder_2_out29), .clk(clk), .reset(reset),
    .Read_Data_1(R29_read_data_1));
  Macro u_R30 (
    .Read_Register_1(Write_Data), .Especial(r30), .Write(decoder_2_out30), .clk(clk), .reset(reset),
    .Read_Data_1(R30_read_data_1));
  Macro u_R31 (
    .Read_Register_1(Write_Data), .Especial(r31), .Write(decoder_2_out31), .clk(clk), .reset(reset),
    .Read_Data_1(R31_read_data_1));
  Multiplexer #(.select(5), .width(32), .enable("false")) multiplexer_1 (
    .in0({32{1'b0}}), .in1(R1_read_data_1), .in2(R2_read_data_1), .in3(R3_read_data_1), .in4(R4_read_data_1),
    .in5(R5_read_data_1), .in6(R6_read_data_1), .in7(R7_read_data_1), .in8(R8_read_data_1),
    .in9(R9_read_data_1), .in10(R10_read_data_1), .in11(R11_read_data_1), .in12(R12_read_data_1),
    .in13(R13_read_data_1), .in14(R14_read_data_1), .in15(R15_read_data_1), .in16(R16_read_data_1),
    .in17(R17_read_data_1), .in18(R18_read_data_1), .in19(R19_read_data_1), .in20(R20_read_data_1),
    .in21(R21_read_data_1), .in22(R22_read_data_1), .in23(R23_read_data_1), .in24(R24_read_data_1),
    .in25(R25_read_data_1), .in26(R26_read_data_1), .in27(R27_read_data_1), .in28(R28_read_data_1),
    .in29(R29_read_data_1), .in30(R30_read_data_1), .in31(R31_read_data_1), .out(Read_Data_1),
    .sel(Read_Register_1));
  Multiplexer #(.select(5), .width(32), .enable("false")) multiplexer_2 (
    .in0({32{1'b0}}), .in1(R1_read_data_1), .in2(R2_read_data_1), .in3(R3_read_data_1), .in4(R4_read_data_1),
    .in5(R5_read_data_1), .in6(R6_read_data_1), .in7(R7_read_data_1), .in8(R8_read_data_1),
    .in9(R9_read_data_1), .in10(R10_read_data_1), .in11(R11_read_data_1), .in12(R12_read_data_1),
    .in13(R13_read_data_1), .in14(R14_read_data_1), .in15(R15_read_data_1), .in16(R16_read_data_1),
    .in17(R17_read_data_1), .in18(R18_read_data_1), .in19(R19_read_data_1), .in20(R20_read_data_1),
    .in21(R21_read_data_1), .in22(R22_read_data_1), .in23(R23_read_data_1), .in24(R24_read_data_1),
    .in25(R25_read_data_1), .in26(R26_read_data_1), .in27(R27_read_data_1), .in28(R28_read_data_1),
    .in29(R29_read_data_1), .in30(R30_read_data_1), .in31(R31_read_data_1), .out(Read_Data_2),
    .sel(Read_Register_2));
endmodule

module ALU (
  input  [3:0] Operation,
  input  [31:0] A,
  input  [31:0] B,
  output Z,
  output [31:0] Result
);

  wire and_2_out;
  wire [0:0] comparator_1_lt;
  wire [31:0] adder_1_out, adder_2_out, and_1_out, conversor_1_salida, conversor_2_salida, multiplexer_1_out,
       multiplexer_2_out, multiplexer_3_out, not_1_out, not_2_out, or_1_out;

  assign not_1_out = ~A;  // NOT_Gate not_1, 32 bits wide
  assign not_2_out = ~B;  // NOT_Gate not_2, 32 bits wide
  Comparator #(.width(32)) comparator_1 (.a(A), .b(B), .lt(comparator_1_lt[0]));  // open: gt, eq
  Multiplexer #(.width(32), .enable("false")) multiplexer_1 (
    .in0(A), .in1(not_1_out), .out(multiplexer_1_out), .sel(Operation[3]));
  Multiplexer #(.width(32), .enable("false")) multiplexer_2 (
    .in0(B), .in1(not_2_out), .out(multiplexer_2_out), .sel(Operation[2]));
  assign and_1_out = multiplexer_1_out & multiplexer_2_out;  // AND_Gate and_1, 32 bits wide
  assign or_1_out = multiplexer_1_out | multiplexer_2_out;  // OR_Gate or_1, 32 bits wide
  Adder #(.width(32)) adder_1 (
    .a(multiplexer_1_out), .b(multiplexer_2_out), .out(adder_1_out), .cin(Operation[2]));  // open: cout
  Multiplexer #(.select(2), .width(32), .enable("false")) multiplexer_3 (
    .in0(and_1_out), .in1(or_1_out), .in2(adder_1_out), .in3({{31{1'b0}}, comparator_1_lt[0]}),
    .out(multiplexer_3_out), .sel(Operation[1:0]));
  and and_2 (and_2_out, ~Operation[3], ~Operation[2], Operation[1], Operation[0]);  // AND_Gate
  nor nor_1 (Z, multiplexer_3_out[0], multiplexer_3_out[1], multiplexer_3_out[2], multiplexer_3_out[3], multiplexer_3_out[4], multiplexer_3_out[5], multiplexer_3_out[6], multiplexer_3_out[7], multiplexer_3_out[8], multiplexer_3_out[9], multiplexer_3_out[10], multiplexer_3_out[11], multiplexer_3_out[12], multiplexer_3_out[13], multiplexer_3_out[14], multiplexer_3_out[15], multiplexer_3_out[16], multiplexer_3_out[17], multiplexer_3_out[18], multiplexer_3_out[19], multiplexer_3_out[20], multiplexer_3_out[21], multiplexer_3_out[22], multiplexer_3_out[23], multiplexer_3_out[24], multiplexer_3_out[25], multiplexer_3_out[26], multiplexer_3_out[27], multiplexer_3_out[28], multiplexer_3_out[29], multiplexer_3_out[30], multiplexer_3_out[31]);
  Multiplexer #(.width(32), .enable("false")) multiplexer_4 (
    .in0(multiplexer_3_out), .in1(adder_2_out), .out(Result), .sel(and_2_out));
  Conversor conversor_1 (.Entrada(B), .Salida(conversor_1_salida));
  Conversor conversor_2 (.Entrada(A), .Salida(conversor_2_salida));
  Adder #(.width(32)) adder_2 (.a(conversor_2_salida), .b(conversor_1_salida), .out(adder_2_out));  // open: cin, cout

  // Notes on the sheet:
  //   0001    OR
  //   Operation    Function
  //   0000    AND
  //   0010    add
  //   0110    subtract
  //   0111    set on less than
  //   1100    NOR
endmodule

module Data_Memory_32 (
  input  Write,
  input  [31:0] Address,
  input  [31:0] Write_Data,
  input  clk,
  input  reset,
  input  Read,
  output [31:0] Read_Data
);

  wire [9:0] bitselector_1_out;

  BitSelector #(.width(32), .group(10)) bitselector_1 (.in(Address), .out(bitselector_1_out), .sel(2'b00));
  RAM #(.dataWidth(32), .bus("separate"), .Datafile_on_reset("TG00ram.txt")) ram_1 (
    .addr(bitselector_1_out[9:2]), .din(Write_Data), .data(Read_Data), .str(Write), .sel(1'b1), .clk(clk),
    .ld(Read), .clr(reset));

  // Notes on the sheet:
  //   Memoria de 32 bits direccionable a nivel de byte
  //   Tan solo implementadas las 256 primeras posiciones de 32 bits o 1024 bytes
endmodule

module Instruction_memory (
  input  [31:0] Read_address,
  output [31:0] Instruction
);

  wire [6:0] bitselector_1_out;

  BitSelector #(.width(30), .group(7)) bitselector_1 (.in(Read_address[31:2]), .out(bitselector_1_out), .sel(3'b000));
  RAM #(.addrWidth(7), .dataWidth(32), .bus("asynch"), .Datafile_on_reset("TG00rom.txt")) ram_1 (
    .addr(bitselector_1_out), .data(Instruction), .sel(1'b1), .ld(1'b1), .clr(1'b0));
endmodule

module AluControl (
  input  [5:0] IB_5_0,
  input  [2:0] Opalu,
  output [3:0] Op
);

  wire [1:0] or_1_out;
  wire [2:1] not_1_out;

  and and_1 (not_1_out[2], ~Opalu[1], Opalu[0]);  // AND_Gate
  not not_1 (not_1_out[1], Opalu[1]);
  not not_2 (or_1_out[1], IB_5_0[2]);
  or or_1 (or_1_out[0], IB_5_0[0], IB_5_0[3]);
  Multiplexer #(.width(4), .enable("false")) multiplexer_1 (
    .in0({1'b0, not_1_out, Opalu[1]}), .in1({1'b0, IB_5_0[1], or_1_out}), .out(Op), .sel(Opalu[2]));
endmodule

module Unidad_de_Control (
  input  [5:0] Opcode,
  input  z,
  output [1:0] FPC,
  output WR,
  output FDC,
  output FC,
  output FB,
  output RM,
  output WM,
  output [2:0] OPALU,
  output halt,
  output Especial
);

  wire and_1_out, and_2_out, and_8_out, and_9_out;

  or or_1 (FPC[1], Opcode[0], ~Opcode[1]);  // OR_Gate
  and and_1 (and_1_out, Opcode[0], ~Opcode[3]);  // AND_Gate
  nand nand_1 (FPC[0], z, Opcode[2]);
  and and_2 (and_2_out, ~Opcode[2], ~Opcode[1]);  // AND_Gate
  or or_2 (WR, and_1_out, and_2_out);
  not not_1 (FC, Opcode[1]);
  and and_3 (FB, Opcode[1], ~Opcode[4]);  // AND_Gate
  not not_2 (RM, Opcode[3]);
  and and_4 (WM, Opcode[3], ~Opcode[4]);  // AND_Gate
  and and_5 (OPALU[2], ~Opcode[5], ~Opcode[2]);  // AND_Gate
  and and_6 (OPALU[1], ~Opcode[5], ~Opcode[2]);  // AND_Gate
  not not_3 (OPALU[0], Opcode[1]);
  and and_7 (halt, Opcode[5], Opcode[4], Opcode[3], Opcode[2], Opcode[1], Opcode[0]);
  and and_8 (and_8_out, Opcode[5], ~Opcode[4], Opcode[3], ~Opcode[2], Opcode[1], ~Opcode[0]);  // AND_Gate
  or or_3 (Especial, and_8_out, and_9_out);
  and and_9 (and_9_out, ~Opcode[5], Opcode[4], ~Opcode[3], Opcode[2], ~Opcode[1], Opcode[0]);  // AND_Gate

  assign FDC = FC;
endmodule

module Macro (
  input  [31:0] Read_Register_1,
  input  Especial,
  input  reset,
  input  Write,
  input  clk,
  output [31:0] Read_Data_1
);

  wire or_1_out;
  wire [31:0] adder_1_out, multiplexer_1_out;

  Adder #(.width(32)) adder_1 (.a(Read_Data_1), .b(32'h4), .out(adder_1_out));  // open: cin, cout
  Multiplexer #(.width(32), .enable("false")) multiplexer_1 (
    .in0(Read_Register_1), .in1(adder_1_out), .out(multiplexer_1_out), .sel(Especial));
  or or_1 (or_1_out, Especial, Write);
  Register #(.width(32)) register_1 (.D(multiplexer_1_out), .en(or_1_out), .Q(Read_Data_1), .clk(clk), .clr(reset));
endmodule

// Unidad de control
module UCPr2 (
  input  [5:0] Opcode,
  input  Z,
  output [1:0] FPC,
  output WR,
  output halt,
  output FDC,
  output FC,
  output FB,
  output RM,
  output WM,
  output [2:0] OpAlu,
  output ESPECIAL
);

  wire and_1_out, and_2_out, and_3_out, and_4_out, and_5_out, and_9_out, and_11_out, not_1_out, not_2_out,
       not_3_out, not_4_out, not_5_out, not_6_out, not_9_out, not_10_out, not_11_out, not_12_out, not_13_out,
       not_14_out, not_15_out, not_16_out, not_17_out, not_18_out, or_3_out;

  not not_1 (not_1_out, Opcode[1]);
  not not_2 (not_2_out, Opcode[2]);
  not not_3 (not_3_out, Opcode[2]);
  not not_4 (not_4_out, Opcode[1]);
  not not_5 (not_5_out, Opcode[0]);
  not not_6 (not_6_out, Opcode[3]);
  not not_7 (FDC, Opcode[1]);
  not not_8 (FC, Opcode[1]);
  or or_1 (FB, Opcode[0], Opcode[3]);
  not not_9 (not_9_out, Opcode[4]);
  not not_10 (not_10_out, Opcode[3]);
  and and_1 (and_1_out, Opcode[3], Opcode[0]);
  not not_11 (not_11_out, Opcode[5]);
  not not_12 (not_12_out, Opcode[2]);
  not not_13 (not_13_out, Opcode[5]);
  not not_14 (not_14_out, Opcode[2]);
  not not_15 (not_15_out, Opcode[3]);
  not not_16 (not_16_out, Opcode[0]);
  not not_17 (not_17_out, Opcode[0]);
  or or_2 (FPC[1], not_1_out, Opcode[5]);
  or or_3 (or_3_out, not_2_out, Opcode[4]);
  and and_2 (and_2_out, not_3_out, not_4_out);
  and and_3 (and_3_out, Opcode[3], not_5_out);
  and and_4 (and_4_out, Opcode[5], not_6_out);
  and and_5 (and_5_out, not_9_out, not_10_out);
  not not_18 (not_18_out, Opcode[0]);
  or or_4 (WM, and_1_out, Opcode[4]);
  and and_6 (OpAlu[2], not_11_out, not_12_out);
  and and_7 (OpAlu[1], not_13_out, not_14_out);
  and and_8 (OpAlu[0], not_15_out, not_16_out);
  and and_9 (and_9_out, Opcode[3], not_17_out);
  or or_5 (WR, and_2_out, and_3_out, and_4_out);
  or or_6 (RM, and_5_out, not_18_out);
  or or_7 (ESPECIAL, and_9_out, Opcode[4]);
  and and_10 (halt, Opcode[0], Opcode[1], Opcode[2], Opcode[3], Opcode[4], Opcode[5]);
  and and_11 (and_11_out, ~Opcode[5], ~Opcode[4], ~Opcode[3], Opcode[2], ~Opcode[1], ~Opcode[0], ~Z);  // AND_Gate
  or or_8 (FPC[0], or_3_out, and_11_out);
endmodule

module Conversor (
  input  [31:0] Entrada,
  output [31:0] Salida
);

  wire comparator_1_lt;
  wire [31:0] negator_1_out;

  Comparator #(.width(32)) comparator_1 (.a(Entrada), .b({32{1'b0}}), .lt(comparator_1_lt));  // open: gt, eq
  Negator #(.width(32)) negator_1 (.in(Entrada), .out(negator_1_out));
  Multiplexer #(.width(32), .enable("false")) multiplexer_1 (
    .in0(Entrada), .in1(negator_1_out), .out(Salida), .sel(comparator_1_lt));
endmodule
